// Logisim project 4_register.circ as structural Verilog: 1 circuit, main circuit main
module main (
  input  write,
  input  [1:0] write_reg_num,
  input  read_reg_num1,
  input  read_read_num2
);

  Decoder decoder_1 (.sel(write_reg_num[0]), .en(write));  // open: out0, out1
  Register #(.width(32)) register_1 ();  // open: D, en, clk, Q, clr
  // Pins of 1 and 2 bits meet at write_reg_num
endmodule
