// Logisim project Assignment_5_circuit.circ as structural Verilog: 1 circuit, main circuit main
module main (
  input  A,
  input  B,
  input  C,
  input  D,
  output E
);

  wire nor_1_out, xor_1_out;

  nor nor_1 (nor_1_out, D, C, B, A);
  ExactlyOne xor_1 (.out(xor_1_out), .in0(D), .in1(C), .in2(B), .in3(A));
  or or_1 (E, nor_1_out, xor_1_out);
endmodule
