// Logisim project Assignment_6_circuit.circ as structural Verilog: 3 circuits, main circuit FA
module FA (
  input  A,
  input  B,
  input  C,
  output Y0,
  output Y1
);

  wire and_1_out, and_2_out, and_3_out, and_4_out, and_5_out, and_6_out, and_7_out, not_1_out, not_2_out,
       not_3_out;

  not not_1 (not_1_out, A);
  not not_2 (not_2_out, B);
  not not_3 (not_3_out, C);
  and and_1 (and_1_out, not_1_out, B, C);
  and and_2 (and_2_out, A, not_2_out, C);
  and and_3 (and_3_out, A, B, not_3_out);
  and and_4 (and_4_out, A, B, C);
  and and_5 (and_5_out, not_1_out, not_2_out, C);
  and and_6 (and_6_out, not_1_out, B, not_3_out);
  and and_7 (and_7_out, A, not_2_out, not_3_out);
  or or_1 (Y1, and_1_out, and_2_out, and_3_out, and_4_out);
  or or_2 (Y0, and_4_out, and_5_out, and_6_out, and_7_out);
endmodule

module adder_32_bit (
  input  [31:0] A,
  input  [31:0] B,
  input  sub_op,
  input  slt_op,
  output [31:0] out_5,
  output Overflow
);

  wire FA1_y1, FA2_y1, FA3_y1, FA4_y1, FA5_y1, FA6_y1, FA7_y1, FA8_y1, FA9_y1, FA10_y1, FA11_y1, FA12_y1,
       FA13_y1, FA14_y1, FA15_y1, FA16_y1, FA17_y1, FA18_y1, FA19_y1, FA20_y1, FA21_y1, FA22_y1, FA23_y1,
       FA24_y1, FA25_y1, FA26_y1, FA27_y1, FA28_y1, FA29_y1, FA30_y1, FA31_y1, multiplexer_2_out, or_1_out;
  wire [31:0] FA1_y0, multiplexer_1_out, multiplexer_3_out, not_1_out;

  Multiplexer #(.enable("false"), .width(32)) multiplexer_1 (
    .in0(B), .in1(not_1_out), .out(multiplexer_1_out), .sel(or_1_out));
  assign not_1_out = ~B;  // NOT_Gate not_1, 32 bits wide
  or or_1 (or_1_out, sub_op, slt_op);
  Multiplexer #(.enable("false")) multiplexer_2 (.in0(1'b0), .in1(or_1_out), .out(multiplexer_2_out), .sel(or_1_out));
  FA FA1 (.A(A[0]), .B(multiplexer_1_out[0]), .C(multiplexer_2_out), .Y0(FA1_y0[0]), .Y1(FA1_y1));
  FA FA2 (.A(A[1]), .B(multiplexer_1_out[1]), .C(FA1_y1), .Y0(FA1_y0[1]), .Y1(FA2_y1));
  FA FA3 (.A(A[2]), .B(multiplexer_1_out[2]), .C(FA2_y1), .Y0(FA1_y0[2]), .Y1(FA3_y1));
  FA FA4 (.A(A[3]), .B(multiplexer_1_out[3]), .C(FA3_y1), .Y0(FA1_y0[3]), .Y1(FA4_y1));
  FA FA5 (.A(A[4]), .B(multiplexer_1_out[4]), .C(FA4_y1), .Y0(FA1_y0[4]), .Y1(FA5_y1));
  FA FA6 (.A(A[5]), .B(multiplexer_1_out[5]), .C(FA5_y1), .Y0(FA1_y0[5]), .Y1(FA6_y1));
  FA FA7 (.A(A[6]), .B(multiplexer_1_out[6]), .C(FA6_y1), .Y0(FA1_y0[6]), .Y1(FA7_y1));
  FA FA8 (.A(A[7]), .B(multiplexer_1_out[7]), .C(FA7_y1), .Y0(FA1_y0[7]), .Y1(FA8_y1));
  FA FA9 (.A(A[8]), .B(multiplexer_1_out[8]), .C(FA8_y1), .Y0(FA1_y0[8]), .Y1(FA9_y1));
  FA FA10 (.A(A[9]), .B(multiplexer_1_out[9]), .C(FA9_y1), .Y0(FA1_y0[9]), .Y1(FA10_y1));
  FA FA11 (.A(A[10]), .B(multiplexer_1_out[10]), .C(FA10_y1), .Y0(FA1_y0[10]), .Y1(FA11_y1));
  FA FA12 (.A(A[11]), .B(multiplexer_1_out[11]), .C(FA11_y1), .Y0(FA1_y0[11]), .Y1(FA12_y1));
  FA FA13 (.A(A[12]), .B(multiplexer_1_out[12]), .C(FA12_y1), .Y0(FA1_y0[12]), .Y1(FA13_y1));
  FA FA14 (.A(A[13]), .B(multiplexer_1_out[13]), .C(FA13_y1), .Y0(FA1_y0[13]), .Y1(FA14_y1));
  FA FA15 (.A(A[14]), .B(multiplexer_1_out[14]), .C(FA14_y1), .Y0(FA1_y0[14]), .Y1(FA15_y1));
  FA FA16 (.A(A[15]), .B(multiplexer_1_out[15]), .C(FA15_y1), .Y0(FA1_y0[15]), .Y1(FA16_y1));
  FA FA17 (.A(A[16]), .B(multiplexer_1_out[16]), .C(FA16_y1), .Y0(FA1_y0[16]), .Y1(FA17_y1));
  FA FA18 (.A(A[17]), .B(multiplexer_1_out[17]), .C(FA17_y1), .Y0(FA1_y0[17]), .Y1(FA18_y1));
  FA FA19 (.A(A[18]), .B(multiplexer_1_out[18]), .C(FA18_y1), .Y0(FA1_y0[18]), .Y1(FA19_y1));
  FA FA20 (.A(A[19]), .B(multiplexer_1_out[19]), .C(FA19_y1), .Y0(FA1_y0[19]), .Y1(FA20_y1));
  FA FA21 (.A(A[20]), .B(multiplexer_1_out[20]), .C(FA20_y1), .Y0(FA1_y0[20]), .Y1(FA21_y1));
  FA FA22 (.A(A[21]), .B(multiplexer_1_out[21]), .C(FA21_y1), .Y0(FA1_y0[21]), .Y1(FA22_y1));
  FA FA23 (.A(A[22]), .B(multiplexer_1_out[22]), .C(FA22_y1), .Y0(FA1_y0[22]), .Y1(FA23_y1));
  FA FA24 (.A(A[23]), .B(multiplexer_1_out[23]), .C(FA23_y1), .Y0(FA1_y0[23]), .Y1(FA24_y1));
  FA FA25 (.A(A[24]), .B(multiplexer_1_out[24]), .C(FA24_y1), .Y0(FA1_y0[24]), .Y1(FA25_y1));
  FA FA26 (.A(A[25]), .B(multiplexer_1_out[25]), .C(FA25_y1), .Y0(FA1_y0[25]), .Y1(FA26_y1));
  FA FA27 (.A(A[26]), .B(multiplexer_1_out[26]), .C(FA26_y1), .Y0(FA1_y0[26]), .Y1(FA27_y1));
  FA FA28 (.A(A[27]), .B(multiplexer_1_out[27]), .C(FA27_y1), .Y0(FA1_y0[27]), .Y1(FA28_y1));
  FA FA29 (.A(A[28]), .B(multiplexer_1_out[28]), .C(FA28_y1), .Y0(FA1_y0[28]), .Y1(FA29_y1));
  FA FA30 (.A(A[29]), .B(multiplexer_1_out[29]), .C(FA29_y1), .Y0(FA1_y0[29]), .Y1(FA30_y1));
  FA FA31 (.A(A[30]), .B(multiplexer_1_out[30]), .C(FA30_y1), .Y0(FA1_y0[30]), .Y1(FA31_y1));
  FA FA32 (.A(A[31]), .B(multiplexer_1_out[31]), .C(FA31_y1), .Y0(FA1_y0[31]), .Y1(Overflow));
  Multiplexer #(.enable("false"), .width(32)) multiplexer_3 (
    .in0({32{1'b0}}), .in1(32'h1), .out(multiplexer_3_out), .sel(FA1_y0[31]));
  Multiplexer #(.enable("false"), .width(32)) multiplexer_4 (
    .in0(FA1_y0), .in1(multiplexer_3_out), .out(out_5), .sel(slt_op));
endmodule

module alu_32_bit (
  input  [31:0] A,
  input  [31:0] B,
  input  [2:0] opcode,
  output [31:0] out_4
);

  wire [31:0] adder_32_bit_1_out_5, and_1_out, not_1_out, or_1_out, xor_1_out;

  assign and_1_out = A & B;  // AND_Gate and_1, 32 bits wide
  assign or_1_out = A | B;  // OR_Gate or_1, 32 bits wide
  // NoConnect on opcode[2]
  assign xor_1_out = A ^ B;  // XOR_Gate xor_1, 32 bits wide
  assign not_1_out = ~A;  // NOT_Gate not_1, 32 bits wide
  Multiplexer #(.enable("false"), .select(3), .width(32)) multiplexer_1 (
    .in0(and_1_out), .in1(or_1_out), .in2(not_1_out), .in3(xor_1_out), .in4(adder_32_bit_1_out_5),
    .in5(adder_32_bit_1_out_5), .in6(adder_32_bit_1_out_5), .out(out_4), .sel(opcode));  // open: in7
  adder_32_bit adder_32_bit_1 (
    .A(A), .B(B), .sub_op(opcode[0]), .slt_op(opcode[1]), .out_5(adder_32_bit_1_out_5));  // open: Overflow
endmodule
