// Logisim project CPU.circ as structural Verilog: 6 circuits, main circuit ALU
module ALU (
  input  [31:0] A,
  input  [31:0] B,
  input  [2:0] opcode,
  output [31:0] result
);

  wire [31:0] adder32_1_out_5, and_1_out, not_1_out, or_1_out, xor_1_out;

  assign and_1_out = A & B;  // AND_Gate and_1, 32 bits wide
  assign or_1_out = A | B;  // OR_Gate or_1, 32 bits wide
  // NoConnect on opcode[2]
  assign xor_1_out = A ^ B;  // XOR_Gate xor_1, 32 bits wide
  assign not_1_out = ~A;  // NOT_Gate not_1, 32 bits wide
  Multiplexer #(.enable("false"), .select(3), .width(32)) multiplexer_1 (
    .in0(and_1_out), .in1(or_1_out), .in2(not_1_out), .in3(xor_1_out), .in4(adder32_1_out_5),
    .in5(adder32_1_out_5), .in6(adder32_1_out_5), .out(result), .sel(opcode));  // open: in7
  adder32 adder32_1 (.A(A), .B(B), .sub_op(opcode[0]), .slt_op(opcode[1]), .out_5(adder32_1_out_5));  // open: Overflow
endmodule

module FA (
  input  A,
  input  B,
  input  C,
  output Y0,
  output Y1
);

  wire and_1_out, and_2_out, and_3_out, and_4_out, and_5_out, and_6_out, and_7_out, not_1_out, not_2_out,
       not_3_out;

  not not_1 (not_1_out, A);
  not not_2 (not_2_out, B);
  not not_3 (not_3_out, C);
  and and_1 (and_1_out, not_1_out, B, C);
  and and_2 (and_2_out, A, not_2_out, C);
  and and_3 (and_3_out, A, B, not_3_out);
  and and_4 (and_4_out, A, B, C);
  and and_5 (and_5_out, not_1_out, not_2_out, C);
  and and_6 (and_6_out, not_1_out, B, not_3_out);
  and and_7 (and_7_out, A, not_2_out, not_3_out);
  or or_1 (Y1, and_1_out, and_2_out, and_3_out, and_4_out);
  or or_2 (Y0, and_4_out, and_5_out, and_6_out, and_7_out);
endmodule

module adder32 (
  input  [31:0] A,
  input  [31:0] B,
  input  sub_op,
  input  slt_op,
  output [31:0] out_5,
  output Overflow
);

  wire FA1_y1, FA2_y1, FA3_y1, FA4_y1, FA5_y1, FA6_y1, FA7_y1, FA8_y1, FA9_y1, FA10_y1, FA11_y1, FA12_y1,
       FA13_y1, FA14_y1, FA15_y1, FA16_y1, FA17_y1, FA18_y1, FA19_y1, FA20_y1, FA21_y1, FA22_y1, FA23_y1,
       FA24_y1, FA25_y1, FA26_y1, FA27_y1, FA28_y1, FA29_y1, FA30_y1, FA31_y1, multiplexer_2_out, or_1_out;
  wire [31:0] FA1_y0, multiplexer_1_out, multiplexer_3_out, not_1_out;

  Multiplexer #(.enable("false"), .width(32)) multiplexer_1 (
    .in0(B), .in1(not_1_out), .out(multiplexer_1_out), .sel(or_1_out));
  assign not_1_out = ~B;  // NOT_Gate not_1, 32 bits wide
  or or_1 (or_1_out, sub_op, slt_op);
  Multiplexer #(.enable("false")) multiplexer_2 (.in0(1'b0), .in1(or_1_out), .out(multiplexer_2_out), .sel(or_1_out));
  FA FA1 (.A(A[0]), .B(multiplexer_1_out[0]), .C(multiplexer_2_out), .Y0(FA1_y0[0]), .Y1(FA1_y1));
  FA FA2 (.A(A[1]), .B(multiplexer_1_out[1]), .C(FA1_y1), .Y0(FA1_y0[1]), .Y1(FA2_y1));
  FA FA3 (.A(A[2]), .B(multiplexer_1_out[2]), .C(FA2_y1), .Y0(FA1_y0[2]), .Y1(FA3_y1));
  FA FA4 (.A(A[3]), .B(multiplexer_1_out[3]), .C(FA3_y1), .Y0(FA1_y0[3]), .Y1(FA4_y1));
  FA FA5 (.A(A[4]), .B(multiplexer_1_out[4]), .C(FA4_y1), .Y0(FA1_y0[4]), .Y1(FA5_y1));
  FA FA6 (.A(A[5]), .B(multiplexer_1_out[5]), .C(FA5_y1), .Y0(FA1_y0[5]), .Y1(FA6_y1));
  FA FA7 (.A(A[6]), .B(multiplexer_1_out[6]), .C(FA6_y1), .Y0(FA1_y0[6]), .Y1(FA7_y1));
  FA FA8 (.A(A[7]), .B(multiplexer_1_out[7]), .C(FA7_y1), .Y0(FA1_y0[7]), .Y1(FA8_y1));
  FA FA9 (.A(A[8]), .B(multiplexer_1_out[8]), .C(FA8_y1), .Y0(FA1_y0[8]), .Y1(FA9_y1));
  FA FA10 (.A(A[9]), .B(multiplexer_1_out[9]), .C(FA9_y1), .Y0(FA1_y0[9]), .Y1(FA10_y1));
  FA FA11 (.A(A[10]), .B(multiplexer_1_out[10]), .C(FA10_y1), .Y0(FA1_y0[10]), .Y1(FA11_y1));
  FA FA12 (.A(A[11]), .B(multiplexer_1_out[11]), .C(FA11_y1), .Y0(FA1_y0[11]), .Y1(FA12_y1));
  FA FA13 (.A(A[12]), .B(multiplexer_1_out[12]), .C(FA12_y1), .Y0(FA1_y0[12]), .Y1(FA13_y1));
  FA FA14 (.A(A[13]), .B(multiplexer_1_out[13]), .C(FA13_y1), .Y0(FA1_y0[13]), .Y1(FA14_y1));
  FA FA15 (.A(A[14]), .B(multiplexer_1_out[14]), .C(FA14_y1), .Y0(FA1_y0[14]), .Y1(FA15_y1));
  FA FA16 (.A(A[15]), .B(multiplexer_1_out[15]), .C(FA15_y1), .Y0(FA1_y0[15]), .Y1(FA16_y1));
  FA FA17 (.A(A[16]), .B(multiplexer_1_out[16]), .C(FA16_y1), .Y0(FA1_y0[16]), .Y1(FA17_y1));
  FA FA18 (.A(A[17]), .B(multiplexer_1_out[17]), .C(FA17_y1), .Y0(FA1_y0[17]), .Y1(FA18_y1));
  FA FA19 (.A(A[18]), .B(multiplexer_1_out[18]), .C(FA18_y1), .Y0(FA1_y0[18]), .Y1(FA19_y1));
  FA FA20 (.A(A[19]), .B(multiplexer_1_out[19]), .C(FA19_y1), .Y0(FA1_y0[19]), .Y1(FA20_y1));
  FA FA21 (.A(A[20]), .B(multiplexer_1_out[20]), .C(FA20_y1), .Y0(FA1_y0[20]), .Y1(FA21_y1));
  FA FA22 (.A(A[21]), .B(multiplexer_1_out[21]), .C(FA21_y1), .Y0(FA1_y0[21]), .Y1(FA22_y1));
  FA FA23 (.A(A[22]), .B(multiplexer_1_out[22]), .C(FA22_y1), .Y0(FA1_y0[22]), .Y1(FA23_y1));
  FA FA24 (.A(A[23]), .B(multiplexer_1_out[23]), .C(FA23_y1), .Y0(FA1_y0[23]), .Y1(FA24_y1));
  FA FA25 (.A(A[24]), .B(multiplexer_1_out[24]), .C(FA24_y1), .Y0(FA1_y0[24]), .Y1(FA25_y1));
  FA FA26 (.A(A[25]), .B(multiplexer_1_out[25]), .C(FA25_y1), .Y0(FA1_y0[25]), .Y1(FA26_y1));
  FA FA27 (.A(A[26]), .B(multiplexer_1_out[26]), .C(FA26_y1), .Y0(FA1_y0[26]), .Y1(FA27_y1));
  FA FA28 (.A(A[27]), .B(multiplexer_1_out[27]), .C(FA27_y1), .Y0(FA1_y0[27]), .Y1(FA28_y1));
  FA FA29 (.A(A[28]), .B(multiplexer_1_out[28]), .C(FA28_y1), .Y0(FA1_y0[28]), .Y1(FA29_y1));
  FA FA30 (.A(A[29]), .B(multiplexer_1_out[29]), .C(FA29_y1), .Y0(FA1_y0[29]), .Y1(FA30_y1));
  FA FA31 (.A(A[30]), .B(multiplexer_1_out[30]), .C(FA30_y1), .Y0(FA1_y0[30]), .Y1(FA31_y1));
  FA FA32 (.A(A[31]), .B(multiplexer_1_out[31]), .C(FA31_y1), .Y0(FA1_y0[31]), .Y1(Overflow));
  Multiplexer #(.enable("false"), .width(32)) multiplexer_3 (
    .in0({32{1'b0}}), .in1(32'h1), .out(multiplexer_3_out), .sel(FA1_y0[31]));
  Multiplexer #(.enable("false"), .width(32)) multiplexer_4 (
    .in0(FA1_y0), .in1(multiplexer_3_out), .out(out_5), .sel(slt_op));
endmodule

module RegisterFile (
  input  write,
  input  [4:0] write_reg_num,
  input  [31:0] write_data,
  input  clock,
  input  [4:0] rd_reg_num_1,
  input  [4:0] rd_reg_num_2,
  input  [4:0] disp_reg,
  input  reset,
  output [31:0] read_data_1,
  output [31:0] read_data_2,
  output [31:0] disp_data
);

  wire and_1_out, and_2_out, and_3_out, and_4_out, and_5_out, and_6_out, and_7_out, and_8_out, and_9_out,
       and_10_out, and_11_out, and_12_out, and_13_out, and_14_out, and_15_out, and_16_out, and_17_out,
       and_18_out, and_19_out, and_20_out, and_21_out, and_22_out, and_23_out, and_24_out, and_25_out,
       and_26_out, and_27_out, and_28_out, and_29_out, and_30_out, and_31_out, decoder_1_out1,
       decoder_1_out2, decoder_1_out3, decoder_1_out4, decoder_1_out5, decoder_1_out6, decoder_1_out7,
       decoder_1_out8, decoder_1_out9, decoder_1_out10, decoder_1_out11, decoder_1_out12, decoder_1_out13,
       decoder_1_out14, decoder_1_out15, decoder_1_out16, decoder_1_out17, decoder_1_out18, decoder_1_out19,
       decoder_1_out20, decoder_1_out21, decoder_1_out22, decoder_1_out23, decoder_1_out24, decoder_1_out25,
       decoder_1_out26, decoder_1_out27, decoder_1_out28, decoder_1_out29, decoder_1_out30, decoder_1_out31;
  wire [31:0] register_1_q, register_2_q, register_3_q, register_4_q, register_5_q, register_6_q,
       register_7_q, register_8_q, register_9_q, register_10_q, register_11_q, register_12_q, register_13_q,
       register_14_q, register_15_q, register_16_q, register_17_q, register_18_q, register_19_q,
       register_20_q, register_21_q, register_22_q, register_23_q, register_24_q, register_25_q,
       register_26_q, register_27_q, register_28_q, register_29_q, register_30_q, register_31_q;

  Decoder #(.select(5)) decoder_1 (
    .out1(decoder_1_out1), .out2(decoder_1_out2), .out3(decoder_1_out3), .out4(decoder_1_out4),
    .out5(decoder_1_out5), .out6(decoder_1_out6), .out7(decoder_1_out7), .out8(decoder_1_out8),
    .out9(decoder_1_out9), .out10(decoder_1_out10), .out11(decoder_1_out11), .out12(decoder_1_out12),
    .out13(decoder_1_out13), .out14(decoder_1_out14), .out15(decoder_1_out15), .out16(decoder_1_out16),
    .out17(decoder_1_out17), .out18(decoder_1_out18), .out19(decoder_1_out19), .out20(decoder_1_out20),
    .out21(decoder_1_out21), .out22(decoder_1_out22), .out23(decoder_1_out23), .out24(decoder_1_out24),
    .out25(decoder_1_out25), .out26(decoder_1_out26), .out27(decoder_1_out27), .out28(decoder_1_out28),
    .out29(decoder_1_out29), .out30(decoder_1_out30), .out31(decoder_1_out31), .sel(write_reg_num), .en(write));  // open: out0
  and and_1 (and_1_out, write, decoder_1_out1);
  and and_2 (and_2_out, write, decoder_1_out2);
  and and_3 (and_3_out, write, decoder_1_out3);
  and and_4 (and_4_out, write, decoder_1_out4);
  and and_5 (and_5_out, write, decoder_1_out5);
  and and_6 (and_6_out, write, decoder_1_out6);
  and and_7 (and_7_out, write, decoder_1_out7);
  and and_8 (and_8_out, write, decoder_1_out8);
  and and_9 (and_9_out, write, decoder_1_out9);
  and and_10 (and_10_out, write, decoder_1_out10);
  and and_11 (and_11_out, write, decoder_1_out11);
  and and_12 (and_12_out, write, decoder_1_out12);
  and and_13 (and_13_out, write, decoder_1_out13);
  and and_14 (and_14_out, write, decoder_1_out14);
  and and_15 (and_15_out, write, decoder_1_out15);
  and and_16 (and_16_out, write, decoder_1_out16);
  and and_17 (and_17_out, write, decoder_1_out17);
  and and_18 (and_18_out, write, decoder_1_out18);
  and and_19 (and_19_out, write, decoder_1_out19);
  and and_20 (and_20_out, write, decoder_1_out20);
  and and_21 (and_21_out, write, decoder_1_out21);
  and and_22 (and_22_out, write, decoder_1_out22);
  and and_23 (and_23_out, write, decoder_1_out23);
  and and_24 (and_24_out, write, decoder_1_out24);
  and and_25 (and_25_out, write, decoder_1_out25);
  and and_26 (and_26_out, write, decoder_1_out26);
  and and_27 (and_27_out, write, decoder_1_out27);
  and and_28 (and_28_out, write, decoder_1_out28);
  and and_29 (and_29_out, write, decoder_1_out29);
  and and_30 (and_30_out, write, decoder_1_out30);
  and and_31 (and_31_out, write, decoder_1_out31);
  Register #(.width(32)) register_1 (.D(write_data), .en(and_1_out), .clk(clock), .Q(register_1_q), .clr(reset));
  Register #(.width(32)) register_2 (.D(write_data), .en(and_2_out), .clk(clock), .Q(register_2_q), .clr(reset));
  Register #(.width(32)) register_3 (.D(write_data), .en(and_3_out), .clk(clock), .Q(register_3_q), .clr(reset));
  Register #(.width(32)) register_4 (.D(write_data), .en(and_4_out), .clk(clock), .Q(register_4_q), .clr(reset));
  Register #(.width(32)) register_5 (.D(write_data), .en(and_5_out), .clk(clock), .Q(register_5_q), .clr(reset));
  Register #(.width(32)) register_6 (.D(write_data), .en(and_6_out), .clk(clock), .Q(register_6_q), .clr(reset));
  Register #(.width(32)) register_7 (.D(write_data), .en(and_7_out), .clk(clock), .Q(register_7_q), .clr(reset));
  Register #(.width(32)) register_8 (.D(write_data), .en(and_8_out), .clk(clock), .Q(register_8_q), .clr(reset));
  Register #(.width(32)) register_9 (.D(write_data), .en(and_9_out), .clk(clock), .Q(register_9_q), .clr(reset));
  Register #(.width(32)) register_10 (.D(write_data), .en(and_10_out), .clk(clock), .Q(register_10_q), .clr(reset));
  Register #(.width(32)) register_11 (.D(write_data), .en(and_11_out), .clk(clock), .Q(register_11_q), .clr(reset));
  Register #(.width(32)) register_12 (.D(write_data), .en(and_12_out), .clk(clock), .Q(register_12_q), .clr(reset));
  Register #(.width(32)) register_13 (.D(write_data), .en(and_13_out), .clk(clock), .Q(register_13_q), .clr(reset));
  Register #(.width(32)) register_14 (.D(write_data), .en(and_14_out), .clk(clock), .Q(register_14_q), .clr(reset));
  Register #(.width(32)) register_15 (.D(write_data), .en(and_15_out), .clk(clock), .Q(register_15_q), .clr(reset));
  Register #(.width(32)) register_16 (.D(write_data), .en(and_16_out), .clk(clock), .Q(register_16_q), .clr(reset));
  Register #(.width(32)) register_17 (.D(write_data), .en(and_17_out), .clk(clock), .Q(register_17_q), .clr(reset));
  Register #(.width(32)) register_18 (.D(write_data), .en(and_18_out), .clk(clock), .Q(register_18_q), .clr(reset));
  Register #(.width(32)) register_19 (.D(write_data), .en(and_19_out), .clk(clock), .Q(register_19_q), .clr(reset));
  Register #(.width(32)) register_20 (.D(write_data), .en(and_20_out), .clk(clock), .Q(register_20_q), .clr(reset));
  Register #(.width(32)) register_21 (.D(write_data), .en(and_21_out), .clk(clock), .Q(register_21_q), .clr(reset));
  Register #(.width(32)) register_22 (.D(write_data), .en(and_22_out), .clk(clock), .Q(register_22_q), .clr(reset));
  Register #(.width(32)) register_23 (.D(write_data), .en(and_23_out), .clk(clock), .Q(register_23_q), .clr(reset));
  Register #(.width(32)) register_24 (.D(write_data), .en(and_24_out), .clk(clock), .Q(register_24_q), .clr(reset));
  Register #(.width(32)) register_25 (.D(write_data), .en(and_25_out), .clk(clock), .Q(register_25_q), .clr(reset));
  Register #(.width(32)) register_26 (.D(write_data), .en(and_26_out), .clk(clock), .Q(register_26_q), .clr(reset));
  Register #(.width(32)) register_27 (.D(write_data), .en(and_27_out), .clk(clock), .Q(register_27_q), .clr(reset));
  Register #(.width(32)) register_28 (.D(write_data), .en(and_28_out), .clk(clock), .Q(register_28_q), .clr(reset));
  Register #(.width(32)) register_29 (.D(write_data), .en(and_29_out), .clk(clock), .Q(register_29_q), .clr(reset));
  Register #(.width(32)) register_30 (.D(write_data), .en(and_30_out), .clk(clock), .Q(register_30_q), .clr(reset));
  Register #(.width(32)) register_31 (.D(write_data), .en(and_31_out), .clk(clock), .Q(register_31_q), .clr(reset));
  Multiplexer #(.enable("false"), .select(5), .width(32)) multiplexer_1 (
    .in0({32{1'b0}}), .in1(register_1_q), .in2(register_2_q), .in3(register_3_q), .in4(register_4_q),
    .in5(register_5_q), .in6(register_6_q), .in7(register_7_q), .in8(register_8_q), .in9(register_9_q),
    .in10(register_10_q), .in11(register_11_q), .in12(register_12_q), .in13(register_13_q),
    .in14(register_14_q), .in15(register_15_q), .in16(register_16_q), .in17(register_17_q),
    .in18(register_18_q), .in19(register_19_q), .in20(register_20_q), .in21(register_21_q),
    .in22(register_22_q), .in23(register_23_q), .in24(register_24_q), .in25(register_25_q),
    .in26(register_26_q), .in27(register_27_q), .in28(register_28_q), .in29(register_29_q),
    .in30(register_30_q), .in31(register_31_q), .out(read_data_1), .sel(rd_reg_num_1));
  Multiplexer #(.enable("false"), .select(5), .width(32)) multiplexer_2 (
    .in0({32{1'b0}}), .in1(register_1_q), .in2(register_2_q), .in3(register_3_q), .in4(register_4_q),
    .in5(register_5_q), .in6(register_6_q), .in7(register_7_q), .in8(register_8_q), .in9(register_9_q),
    .in10(register_10_q), .in11(register_11_q), .in12(register_12_q), .in13(register_13_q),
    .in14(register_14_q), .in15(register_15_q), .in16(register_16_q), .in17(register_17_q),
    .in18(register_18_q), .in19(register_19_q), .in20(register_20_q), .in21(register_21_q),
    .in22(register_22_q), .in23(register_23_q), .in24(register_24_q), .in25(register_25_q),
    .in26(register_26_q), .in27(register_27_q), .in28(register_28_q), .in29(register_29_q),
    .in30(register_30_q), .in31(register_31_q), .out(read_data_2), .sel(rd_reg_num_2));
  Multiplexer #(.enable("false"), .select(5), .width(32)) multiplexer_3 (
    .in0({32{1'b0}}), .in1(register_1_q), .in2(register_2_q), .in3(register_3_q), .in4(register_4_q),
    .in5(register_5_q), .in6(register_6_q), .in7(register_7_q), .in8(register_8_q), .in9(register_9_q),
    .in10(register_10_q), .in11(register_11_q), .in12(register_12_q), .in13(register_13_q),
    .in14(register_14_q), .in15(register_15_q), .in16(register_16_q), .in17(register_17_q),
    .in18(register_18_q), .in19(register_19_q), .in20(register_20_q), .in21(register_21_q),
    .in22(register_22_q), .in23(register_23_q), .in24(register_24_q), .in25(register_25_q),
    .in26(register_26_q), .in27(register_27_q), .in28(register_28_q), .in29(register_29_q),
    .in30(register_30_q), .in31(register_31_q), .out(disp_data), .sel(disp_reg));

  // Notes on the sheet:
  //   hard-coded 0 for register $0
endmodule

module CPU (
  input  reset,
  input  [4:0] ViewRegisterNum,
  output [31:0] RegisterContents
);

  wire clock_1_out, control_1_itype, control_1_regwrite;
  wire [2:0] control_1_aluop;
  wire [4:0] multiplexer_1_out;
  wire [7:0] rom_1_p2, rom_1_p3, rom_1_p4, rom_1_p5;
  wire [15:0] adder_1_out, ProgramCounter_q;
  wire [31:0] alu_1_result, bit_extender_1_out, multiplexer_2_out, registerfile_1_read_data_1,
       registerfile_1_read_data_2;

  Register #(.width(16)) ProgramCounter (
    .D(adder_1_out), .en(1'b1), .clk(clock_1_out), .Q(ProgramCounter_q), .clr(reset));
  Clock clock_1 (.out(clock_1_out));
  Adder #(.width(16)) adder_1 (.a(16'h4), .b(ProgramCounter_q), .out(adder_1_out));  // open: cin, cout
  // ROM #(.addrWidth(16), .line("quad")) rom_1: pin names not known; wires that end beside it: ProgramCounter_q, rom_1_p2, rom_1_p3, rom_1_p4, rom_1_p5
  Multiplexer #(.enable("false"), .width(5)) multiplexer_1 (
    .in0(rom_1_p3[7:3]), .in1(rom_1_p4[4:0]), .out(multiplexer_1_out), .sel(control_1_itype));
  control control_1 (
    .opcode(rom_1_p5[7:2]), .funct(rom_1_p2[5:0]), .ALUop(control_1_aluop), .RegWrite(control_1_regwrite),
    .IType(control_1_itype));
  assign bit_extender_1_out = {{16{rom_1_p3[7]}}, {rom_1_p3, rom_1_p2}};  // Bit_Extender bit_extender_1
  RegisterFile registerfile_1 (
    .write(control_1_regwrite), .write_reg_num(multiplexer_1_out), .write_data(alu_1_result),
    .clock(clock_1_out), .rd_reg_num_1({rom_1_p5[1:0], rom_1_p4[7:5]}), .rd_reg_num_2(rom_1_p4[4:0]),
    .disp_reg(ViewRegisterNum), .reset(reset), .read_data_1(registerfile_1_read_data_1),
    .read_data_2(registerfile_1_read_data_2), .disp_data(RegisterContents));
  Multiplexer #(.enable("false"), .width(32)) multiplexer_2 (
    .in0(registerfile_1_read_data_2), .in1(bit_extender_1_out), .out(multiplexer_2_out), .sel(control_1_itype));
  ALU alu_1 (.A(registerfile_1_read_data_1), .B(multiplexer_2_out), .opcode(control_1_aluop), .result(alu_1_result));

  // Notes on the sheet:
  //   contents of rom_1 (hex, n*v repeats v):
  //   5 0 8 20 3 0 9 20 20 50 9 1 22 58 9 1 25 60 4b 1 2a 68 c 0 26 70 8d 1 24 78 ae 1 1 0 e8 31 0 0 9 35
  //   0 0 2a 39 a 0 2b 29
  //   opcode
  //   constant
  //   rt
  //   rs
  //   func
  //   shamt
  //   rd
endmodule

module control (
  input  [5:0] opcode,
  input  [5:0] funct,
  output [2:0] ALUop,
  output RegWrite,
  output IType
);

  wire and_1_out, and_2_out, and_3_out, and_4_out, and_5_out, and_6_out, not_1_out, not_2_out, not_3_out,
       not_4_out;

  not not_1 (not_1_out, opcode[3]);
  not not_2 (not_2_out, opcode[2]);
  not not_3 (not_3_out, funct[3]);
  not not_4 (not_4_out, funct[2]);
  and and_1 (and_1_out, not_1_out, not_4_out);
  or or_1 (ALUop[2], and_1_out, and_2_out);
  and and_2 (and_2_out, opcode[3], not_2_out);
  and and_3 (and_3_out, not_1_out, funct[2], funct[1]);
  and and_4 (and_4_out, not_1_out, funct[3]);
  or or_2 (ALUop[1], and_3_out, and_4_out, opcode[1]);
  and and_5 (and_5_out, not_1_out, funct[0]);
  and and_6 (and_6_out, not_1_out, not_3_out, funct[1]);
  or or_3 (ALUop[0], and_5_out, and_6_out, opcode[0], opcode[1]);

  assign IType = opcode[3];
  assign RegWrite = 1'b1;
endmodule
