// Logisim project circuit_1.circ as structural Verilog: 1 circuit, main circuit main
module main (
  input  A,
  input  B,
  input  S,
  output C
);

  wire and_1_out, and_2_out, not_1_out;

  and and_1 (and_1_out, A, S);
  and and_2 (and_2_out, B, not_1_out);
  not not_1 (not_1_out, S);
  or or_1 (C, and_1_out, and_2_out);
endmodule
