// Logisim project srdh.circ as structural Verilog: 1 circuit, main circuit main
module main (
  input  reset,
  output [31:0] out_2
);

  wire clock_1_out;
  wire [15:0] adder_1_out, register_1_q;

  Register #(.width(16)) register_1 (.D(adder_1_out), .en(1'b1), .clk(clock_1_out), .Q(register_1_q), .clr(reset));
  Clock clock_1 (.out(clock_1_out));
  // ROM #(.addrWidth(16), .line("quad")) rom_1: pin names not known; wires that end beside it: register_1_q
  Adder #(.width(16)) adder_1 (.a(16'h4), .b(register_1_q), .out(adder_1_out));  // open: cin, cout

  // Notes on the sheet:
  //   contents of rom_1 (hex, n*v repeats v):
  //   1 2 3 4 5 6 7 8 a b c d e f
endmodule
