// Logisim project sum_of_prod.circ as structural Verilog: 3 circuits, main circuit FA
module FA (
  input  A,
  input  B,
  input  C,
  output Y1,
  output Y0
);

  wire and_1_out, and_2_out, and_3_out, and_4_out, and_5_out, and_6_out, and_7_out, not_1_out, not_2_out,
       not_3_out;

  not not_1 (not_1_out, A);
  not not_2 (not_2_out, B);
  not not_3 (not_3_out, C);
  and and_1 (and_1_out, not_1_out, B, C);
  and and_2 (and_2_out, A, not_2_out, C);
  and and_3 (and_3_out, A, B, not_3_out);
  and and_4 (and_4_out, A, B, C);
  and and_5 (and_5_out, not_1_out, not_2_out, C);
  and and_6 (and_6_out, not_1_out, B, not_3_out);
  and and_7 (and_7_out, A, not_2_out, not_3_out);
  or or_1 (Y1, and_1_out, and_2_out, and_3_out, and_4_out);
  or or_2 (Y0, and_4_out, and_5_out, and_6_out, and_7_out);
endmodule

module adder4bit (
  input  [3:0] A,
  input  [3:0] B,
  input  sub_op,
  input  slt_op,
  output [3:0] out_5,
  output Overflow
);

  wire fa_1_y1, fa_2_y1, fa_3_y1, multiplexer_1_out, or_1_out;
  wire [3:0] fa_1_y0, multiplexer_2_out, multiplexer_3_out, not_1_out;

  assign not_1_out = ~B;  // NOT_Gate not_1, 4 bits wide
  Multiplexer #(.enable("false")) multiplexer_1 (.in0(1'b0), .in1(1'b1), .out(multiplexer_1_out), .sel(or_1_out));
  Multiplexer #(.enable("false"), .width(4)) multiplexer_2 (
    .in0(B), .in1(not_1_out), .out(multiplexer_2_out), .sel(or_1_out));
  or or_1 (or_1_out, sub_op, slt_op);
  FA fa_1 (.A(A[0]), .B(multiplexer_2_out[0]), .C(multiplexer_1_out), .Y1(fa_1_y1), .Y0(fa_1_y0[0]));
  FA fa_2 (.A(A[1]), .B(multiplexer_2_out[1]), .C(fa_1_y1), .Y1(fa_2_y1), .Y0(fa_1_y0[1]));
  FA fa_3 (.A(A[2]), .B(multiplexer_2_out[2]), .C(fa_2_y1), .Y1(fa_3_y1), .Y0(fa_1_y0[2]));
  FA fa_4 (.A(A[3]), .B(multiplexer_2_out[3]), .C(fa_3_y1), .Y1(Overflow), .Y0(fa_1_y0[3]));
  Multiplexer #(.enable("false"), .width(4)) multiplexer_3 (
    .in0(4'b0000), .in1(4'b0001), .out(multiplexer_3_out), .sel(fa_1_y0[3]));
  Multiplexer #(.enable("false"), .width(4)) multiplexer_4 (
    .in0(fa_1_y0), .in1(multiplexer_3_out), .out(out_5), .sel(slt_op));
endmodule

module alu (
  input  [3:0] A,
  input  [3:0] B,
  input  [2:0] OP,
  output [3:0] out_4
);

  wire [3:0] adder4bit_1_out_5, and_1_out, not_1_out, or_1_out, xor_1_out;

  // NoConnect on OP[2]
  assign and_1_out = A & B;  // AND_Gate and_1, 4 bits wide
  assign or_1_out = A | B;  // OR_Gate or_1, 4 bits wide
  assign xor_1_out = A ^ B;  // XOR_Gate xor_1, 4 bits wide
  assign not_1_out = ~A;  // NOT_Gate not_1, 4 bits wide
  Multiplexer #(.enable("false"), .select(3), .width(4)) multiplexer_1 (
    .in0(and_1_out), .in1(or_1_out), .in2(xor_1_out), .in3(not_1_out), .in4(adder4bit_1_out_5),
    .in5(adder4bit_1_out_5), .in6(adder4bit_1_out_5), .out(out_4), .sel(OP));  // open: in7
  adder4bit adder4bit_1 (.A(A), .B(B), .sub_op(OP[0]), .slt_op(OP[1]), .out_5(adder4bit_1_out_5));  // open: Overflow
endmodule
